// Logisim project circuit.circ as structural Verilog: 1 circuit, main circuit myXOR
module myXOR (
  input  x,
  input  in_2,
  input  y
);

  wire and_1_out, and_2_out, not_1_out, not_2_out, or_1_out;

  not not_1 (not_1_out, x);
  not not_2 (not_2_out, y);
  and and_1 (and_1_out, not_1_out, y);
  and and_2 (and_2_out, x, not_2_out);
  or or_1 (or_1_out, and_1_out, and_2_out);
endmodule
